// Logisim project Processor.circ as structural Verilog
module main (
  output overflow,
  output [17:0] out_2
);

  wire and_1_out, and_2_out, and_3_out, branch, clock, controlunit_1_load, controlunit_1_src1,
       controlunit_1_src2, controlunit_1_store, controlunit_1_we, jump, n18bitcomparator_1_eq,
       n18bitcomparator_1_gt, n18bitcomparator_1_lt, or_1_out, PcEnable, producenzp_1_n, producenzp_1_p,
       producenzp_1_z;
  wire [3:0] multiplexer_3_out, multiplexer_4_out;
  wire [13:0] adder_1_out, adder_2_out, bit_extender_1_out, bit_extender_3_out, counter_1_q,
       multiplexer_1_out, multiplexer_2_out;
  wire [17:0] bit_extender_2_out, multiplexer_5_out, multiplexer_6_out, n18bitalu_1_result, ram_1_data,
       register_file_1_outdata1, register_file_1_outdata2;

  Multiplexer #(.width(14), .enable("false")) multiplexer_1 (
    .in0(adder_2_out), .in1(multiplexer_2_out), .out(multiplexer_1_out), .sel(branch));
  Counter #(.width(14), .max('h3fff)) counter_1 (
    .load(jump), .D(multiplexer_1_out), .count(PcEnable), .Q(counter_1_q), .clk(clock));  // open: carry, clr
  Multiplexer #(.width(14), .enable("false")) multiplexer_2 (
    .in0(counter_1_q), .in1(adder_1_out), .out(multiplexer_2_out), .sel(or_1_out));
  assign bit_extender_1_out = {{8{out_2[17]}}, out_2[17:12]};  // Bit_Extender bit_extender_1
  Adder #(.width(14)) adder_1 (.a(counter_1_q), .b(bit_extender_1_out), .out(adder_1_out));  // open: cin, cout
  ROM #(.addrWidth(14), .dataWidth(18)) rom_1 (.addr(counter_1_q), .data(out_2));  // open: sel
  Adder #(.width(14)) adder_2 (.a(counter_1_q), .b(out_2[17:4]), .out(adder_2_out));  // open: cin, cout
  assign bit_extender_2_out = {{12{out_2[17]}}, out_2[17:12]};  // Bit_Extender bit_extender_2
  ControlUnit controlunit_1 (
    .in_1(clock), .opcode(out_2[3:0]), .PcEnable(PcEnable), .we(controlunit_1_we), .Load(controlunit_1_load),
    .src1(controlunit_1_src1), .src2(controlunit_1_src2), .store(controlunit_1_store), .jump(jump),
    .brach(branch));
  _18bitComparator u_18bitcomparator_1 (
    .in_1(register_file_1_outdata1), .in_2(register_file_1_outdata2), .gt(n18bitcomparator_1_gt),
    .eq(n18bitcomparator_1_eq), .lt(n18bitcomparator_1_lt));
  produceNZP producenzp_1 (.Opcode(out_2[3:0]), .n(producenzp_1_n), .z(producenzp_1_z), .p(producenzp_1_p));
  and and_1 (and_1_out, producenzp_1_p, n18bitcomparator_1_gt);
  and and_2 (and_2_out, n18bitcomparator_1_eq, producenzp_1_z);
  and and_3 (and_3_out, producenzp_1_n, n18bitcomparator_1_lt);
  Multiplexer #(.width(4), .enable("false")) multiplexer_3 (
    .in0(out_2[11:8]), .in1(out_2[7:4]), .out(multiplexer_3_out), .sel(controlunit_1_src1));
  Multiplexer #(.width(4), .enable("false")) multiplexer_4 (
    .in0(out_2[15:12]), .in1(out_2[11:8]), .out(multiplexer_4_out), .sel(controlunit_1_src2));
  Clock clock_1 (.out(clock));
  or or_1 (or_1_out, and_1_out, and_2_out, and_3_out);
  Multiplexer #(.width(18), .enable("false")) multiplexer_5 (
    .in0(n18bitalu_1_result), .in1(ram_1_data), .out(multiplexer_5_out), .sel(controlunit_1_load));
  register_file register_file_1 (
    .src1(multiplexer_3_out), .src2(multiplexer_4_out), .dest(out_2[7:4]), .inData(multiplexer_5_out),
    .WriteEnable(controlunit_1_we), .clock(clock), .outdata1(register_file_1_outdata1),
    .outdata2(register_file_1_outdata2));
  Multiplexer #(.width(18), .enable("false")) multiplexer_6 (
    .in0(register_file_1_outdata2), .in1(bit_extender_2_out), .out(multiplexer_6_out), .sel(out_2[0]));
  _18bitALU u_18bitalu_1 (
    .Operand_A(register_file_1_outdata1), .Operand_B(multiplexer_6_out), .Operation(out_2[2:1]),
    .Carry_In(1'b0), .result(n18bitalu_1_result), .overflow(overflow));
  assign bit_extender_3_out = {{4{1'b0}}, out_2[17:8]};  // Bit_Extender bit_extender_3
  RAM #(.addrWidth(14), .dataWidth(18), .bus("separate")) ram_1 (
    .addr(bit_extender_3_out), .din(register_file_1_outdata1), .data(ram_1_data), .str(controlunit_1_store),
    .clk(clock));  // open: sel, ld, clr

  // Notes on the sheet:
  //   contents of rom_1 (hex, n*v repeats v):
  //   0 118 120 7231 4344 4356 1465 1577 1783 f89 178c ca 3e78d 8*0 2356
endmodule

module _1_bit_register (
  input  \input ,
  input  eneable,
  input  clock,
  output \output 
);

  wire multiplexer_1_out;

  Multiplexer #(.enable("false")) multiplexer_1 (.in0(\output ), .in1(\input ), .out(multiplexer_1_out), .sel(eneable));
  d_latch d_latch_1 (.\input (multiplexer_1_out), .clock(clock), .Q(\output ));
endmodule

module d_latch (
  input  \input ,
  input  clock,
  output Q
);

  wire and_1_out, and_2_out, nor_1_out, not_1_out;

  not not_1 (not_1_out, \input );
  and and_1 (and_1_out, \input , clock);
  and and_2 (and_2_out, clock, not_1_out);
  nor nor_1 (nor_1_out, and_1_out, Q);
  nor nor_2 (Q, nor_1_out, and_2_out);
endmodule

module flip_flop (
  input  \input ,
  input  clock,
  output Q
);

  wire d_latch_1_q, not_1_out;

  d_latch d_latch_1 (.\input (\input ), .clock(clock), .Q(d_latch_1_q));
  not not_1 (not_1_out, clock);
  d_latch d_latch_2 (.\input (d_latch_1_q), .clock(not_1_out), .Q(Q));
endmodule

module _18_bit_register (
  input  [17:0] \input ,
  input  enable,
  input  clock,
  output [17:0] \output 
);

  _1_bit_register u_1_bit_register_1 (.\input (\input [0]), .eneable(enable), .clock(clock), .\output (\output [0]));
  _1_bit_register u_1_bit_register_2 (.\input (\input [1]), .eneable(enable), .clock(clock), .\output (\output [1]));
  _1_bit_register u_1_bit_register_3 (.\input (\input [3]), .eneable(enable), .clock(clock), .\output (\output [3]));
  _1_bit_register u_1_bit_register_4 (.\input (\input [2]), .eneable(enable), .clock(clock), .\output (\output [2]));
  _1_bit_register u_1_bit_register_5 (.\input (\input [4]), .eneable(enable), .clock(clock), .\output (\output [4]));
  _1_bit_register u_1_bit_register_6 (.\input (\input [5]), .eneable(enable), .clock(clock), .\output (\output [5]));
  _1_bit_register u_1_bit_register_7 (.\input (\input [6]), .eneable(enable), .clock(clock), .\output (\output [6]));
  _1_bit_register u_1_bit_register_8 (.\input (\input [8]), .eneable(enable), .clock(clock), .\output (\output [8]));
  _1_bit_register u_1_bit_register_9 (.\input (\input [7]), .eneable(enable), .clock(clock), .\output (\output [7]));
  _1_bit_register u_1_bit_register_10 (.\input (\input [9]), .eneable(enable), .clock(clock), .\output (\output [9]));
  _1_bit_register u_1_bit_register_11 (.\input (\input [10]), .eneable(enable), .clock(clock), .\output (\output [10]));
  _1_bit_register u_1_bit_register_12 (.\input (\input [11]), .eneable(enable), .clock(clock), .\output (\output [11]));
  _1_bit_register u_1_bit_register_13 (.\input (\input [12]), .eneable(enable), .clock(clock), .\output (\output [12]));
  _1_bit_register u_1_bit_register_14 (.\input (\input [13]), .eneable(enable), .clock(clock), .\output (\output [13]));
  _1_bit_register u_1_bit_register_15 (.\input (\input [14]), .eneable(enable), .clock(clock), .\output (\output [14]));
  _1_bit_register u_1_bit_register_16 (.\input (\input [16]), .eneable(enable), .clock(clock), .\output (\output [16]));
  _1_bit_register u_1_bit_register_17 (.\input (\input [15]), .eneable(enable), .clock(clock), .\output (\output [15]));
  _1_bit_register u_1_bit_register_18 (.\input (\input [17]), .eneable(enable), .clock(clock), .\output (\output [17]));
endmodule

// R file
module register_file (
  input  [3:0] src1,
  input  [3:0] src2,
  input  [3:0] dest,
  input  [17:0] inData,
  input  WriteEnable,
  input  clock,
  output [17:0] outdata1,
  output [17:0] outdata2
);

  wire and_1_out, and_2_out, and_3_out, and_4_out, and_5_out, and_6_out, and_7_out, and_8_out, and_9_out,
       and_10_out, and_11_out, and_12_out, and_13_out, and_14_out, and_15_out, and_16_out, decoder_1_out0,
       decoder_1_out1, decoder_1_out2, decoder_1_out3, decoder_1_out4, decoder_1_out5, decoder_1_out6,
       decoder_1_out7, decoder_1_out8, decoder_1_out9, decoder_1_out10, decoder_1_out11, decoder_1_out12,
       decoder_1_out13, decoder_1_out14, decoder_1_out15, decoder_2_out0, decoder_2_out1, decoder_2_out2,
       decoder_2_out3, decoder_2_out4, decoder_2_out5, decoder_2_out6, decoder_2_out7, decoder_2_out8,
       decoder_2_out9, decoder_2_out10, decoder_2_out11, decoder_2_out12, decoder_2_out13, decoder_2_out14,
       decoder_2_out15, decoder_3_out0, decoder_3_out1, decoder_3_out2, decoder_3_out3, decoder_3_out4,
       decoder_3_out5, decoder_3_out6, decoder_3_out7, decoder_3_out8, decoder_3_out9, decoder_3_out10,
       decoder_3_out11, decoder_3_out12, decoder_3_out13, decoder_3_out14, decoder_3_out15;
  wire [17:0] register_1_q, register_2_q, register_3_q, register_4_q, register_5_q, register_6_q,
       register_7_q, register_8_q, register_9_q, register_10_q, register_11_q, register_12_q, register_13_q,
       register_14_q, register_15_q, register_16_q;

  Decoder #(.select(4), .enable("false")) decoder_1 (
    .out0(decoder_1_out0), .out1(decoder_1_out1), .out2(decoder_1_out2), .out3(decoder_1_out3),
    .out4(decoder_1_out4), .out5(decoder_1_out5), .out6(decoder_1_out6), .out7(decoder_1_out7),
    .out8(decoder_1_out8), .out9(decoder_1_out9), .out10(decoder_1_out10), .out11(decoder_1_out11),
    .out12(decoder_1_out12), .out13(decoder_1_out13), .out14(decoder_1_out14), .out15(decoder_1_out15),
    .sel(src1));
  Decoder #(.select(4), .enable("false")) decoder_2 (
    .out0(decoder_2_out0), .out1(decoder_2_out1), .out2(decoder_2_out2), .out3(decoder_2_out3),
    .out4(decoder_2_out4), .out5(decoder_2_out5), .out6(decoder_2_out6), .out7(decoder_2_out7),
    .out8(decoder_2_out8), .out9(decoder_2_out9), .out10(decoder_2_out10), .out11(decoder_2_out11),
    .out12(decoder_2_out12), .out13(decoder_2_out13), .out14(decoder_2_out14), .out15(decoder_2_out15),
    .sel(src2));
  Decoder #(.select(4), .enable("false")) decoder_3 (
    .out0(decoder_3_out0), .out1(decoder_3_out1), .out2(decoder_3_out2), .out3(decoder_3_out3),
    .out4(decoder_3_out4), .out5(decoder_3_out5), .out6(decoder_3_out6), .out7(decoder_3_out7),
    .out8(decoder_3_out8), .out9(decoder_3_out9), .out10(decoder_3_out10), .out11(decoder_3_out11),
    .out12(decoder_3_out12), .out13(decoder_3_out13), .out14(decoder_3_out14), .out15(decoder_3_out15),
    .sel(dest));
  Register #(.width(18)) register_1 (.D(inData), .en(and_1_out), .Q(register_1_q), .clk(clock));  // open: clr
  and and_1 (and_1_out, decoder_3_out0, WriteEnable);
  Register #(.width(18)) register_2 (.D(inData), .en(and_2_out), .Q(register_2_q), .clk(clock));  // open: clr
  and and_2 (and_2_out, decoder_3_out1, WriteEnable);
  Register #(.width(18)) register_3 (.D(inData), .en(and_3_out), .Q(register_3_q), .clk(clock));  // open: clr
  and and_3 (and_3_out, decoder_3_out2, WriteEnable);
  Register #(.width(18)) register_4 (.D(inData), .en(and_4_out), .Q(register_4_q), .clk(clock));  // open: clr
  and and_4 (and_4_out, decoder_3_out3, WriteEnable);
  Register #(.width(18)) register_5 (.D(inData), .en(and_5_out), .Q(register_5_q), .clk(clock));  // open: clr
  and and_5 (and_5_out, decoder_3_out4, WriteEnable);
  Register #(.width(18)) register_6 (.D(inData), .en(and_6_out), .Q(register_6_q), .clk(clock));  // open: clr
  and and_6 (and_6_out, decoder_3_out5, WriteEnable);
  Register #(.width(18)) register_7 (.D(inData), .en(and_7_out), .Q(register_7_q), .clk(clock));  // open: clr
  and and_7 (and_7_out, decoder_3_out6, WriteEnable);
  Register #(.width(18)) register_8 (.D(inData), .en(and_8_out), .Q(register_8_q), .clk(clock));  // open: clr
  and and_8 (and_8_out, decoder_3_out7, WriteEnable);
  Register #(.width(18)) register_9 (.D(inData), .en(and_9_out), .Q(register_9_q), .clk(clock));  // open: clr
  and and_9 (and_9_out, decoder_3_out8, WriteEnable);
  Register #(.width(18)) register_10 (.D(inData), .en(and_10_out), .Q(register_10_q), .clk(clock));  // open: clr
  buf and_10 (and_10_out, decoder_3_out9);  // AND_Gate
  Register #(.width(18)) register_11 (.D(inData), .en(and_11_out), .Q(register_11_q), .clk(clock));  // open: clr
  and and_11 (and_11_out, decoder_3_out10, WriteEnable);
  Register #(.width(18)) register_12 (.D(inData), .en(and_12_out), .Q(register_12_q), .clk(clock));  // open: clr
  and and_12 (and_12_out, decoder_3_out11, WriteEnable);
  Register #(.width(18)) register_13 (.D(inData), .en(and_13_out), .Q(register_13_q), .clk(clock));  // open: clr
  and and_13 (and_13_out, decoder_3_out12, WriteEnable);
  Register #(.width(18)) register_14 (.D(inData), .en(and_14_out), .Q(register_14_q), .clk(clock));  // open: clr
  and and_14 (and_14_out, decoder_3_out13, WriteEnable);
  Register #(.width(18)) register_15 (.D(inData), .en(and_15_out), .Q(register_15_q), .clk(clock));  // open: clr
  and and_15 (and_15_out, decoder_3_out14, WriteEnable);
  Register #(.width(18)) register_16 (.D(inData), .en(and_16_out), .Q(register_16_q), .clk(clock));  // open: clr
  and and_16 (and_16_out, decoder_3_out15, WriteEnable);
  assign outdata1 = decoder_1_out0 ? register_1_q : 18'bz;  // Controlled_Buffer controlled_buffer_1
  assign outdata2 = decoder_2_out0 ? register_1_q : 18'bz;  // Controlled_Buffer controlled_buffer_2
  assign outdata1 = decoder_1_out1 ? register_2_q : 18'bz;  // Controlled_Buffer controlled_buffer_3
  assign outdata2 = decoder_2_out1 ? register_2_q : 18'bz;  // Controlled_Buffer controlled_buffer_4
  assign outdata1 = decoder_1_out2 ? register_3_q : 18'bz;  // Controlled_Buffer controlled_buffer_5
  assign outdata2 = decoder_2_out2 ? register_3_q : 18'bz;  // Controlled_Buffer controlled_buffer_6
  assign outdata1 = decoder_1_out3 ? register_4_q : 18'bz;  // Controlled_Buffer controlled_buffer_7
  assign outdata2 = decoder_2_out3 ? register_4_q : 18'bz;  // Controlled_Buffer controlled_buffer_8
  assign outdata1 = decoder_1_out4 ? register_5_q : 18'bz;  // Controlled_Buffer controlled_buffer_9
  assign outdata2 = decoder_2_out4 ? register_5_q : 18'bz;  // Controlled_Buffer controlled_buffer_10
  assign outdata1 = decoder_1_out5 ? register_6_q : 18'bz;  // Controlled_Buffer controlled_buffer_11
  assign outdata2 = decoder_2_out5 ? register_6_q : 18'bz;  // Controlled_Buffer controlled_buffer_12
  assign outdata1 = decoder_1_out6 ? register_7_q : 18'bz;  // Controlled_Buffer controlled_buffer_13
  assign outdata2 = decoder_2_out6 ? register_7_q : 18'bz;  // Controlled_Buffer controlled_buffer_14
  assign outdata1 = decoder_1_out7 ? register_8_q : 18'bz;  // Controlled_Buffer controlled_buffer_15
  assign outdata2 = decoder_2_out7 ? register_8_q : 18'bz;  // Controlled_Buffer controlled_buffer_16
  assign outdata1 = decoder_1_out8 ? register_9_q : 18'bz;  // Controlled_Buffer controlled_buffer_17
  assign outdata2 = decoder_2_out8 ? register_9_q : 18'bz;  // Controlled_Buffer controlled_buffer_18
  assign outdata1 = decoder_1_out9 ? register_10_q : 18'bz;  // Controlled_Buffer controlled_buffer_19
  assign outdata2 = decoder_2_out9 ? register_10_q : 18'bz;  // Controlled_Buffer controlled_buffer_20
  assign outdata1 = decoder_1_out10 ? register_11_q : 18'bz;  // Controlled_Buffer controlled_buffer_21
  assign outdata2 = decoder_2_out10 ? register_11_q : 18'bz;  // Controlled_Buffer controlled_buffer_22
  assign outdata1 = decoder_1_out11 ? register_12_q : 18'bz;  // Controlled_Buffer controlled_buffer_23
  assign outdata2 = decoder_2_out11 ? register_12_q : 18'bz;  // Controlled_Buffer controlled_buffer_24
  assign outdata1 = decoder_1_out12 ? register_13_q : 18'bz;  // Controlled_Buffer controlled_buffer_25
  assign outdata2 = decoder_2_out12 ? register_13_q : 18'bz;  // Controlled_Buffer controlled_buffer_26
  assign outdata1 = decoder_1_out13 ? register_14_q : 18'bz;  // Controlled_Buffer controlled_buffer_27
  assign outdata2 = decoder_2_out13 ? register_14_q : 18'bz;  // Controlled_Buffer controlled_buffer_28
  assign outdata1 = decoder_1_out14 ? register_15_q : 18'bz;  // Controlled_Buffer controlled_buffer_29
  assign outdata2 = decoder_2_out14 ? register_15_q : 18'bz;  // Controlled_Buffer controlled_buffer_30
  assign outdata1 = decoder_1_out15 ? register_16_q : 18'bz;  // Controlled_Buffer controlled_buffer_31
  assign outdata2 = decoder_2_out15 ? register_16_q : 18'bz;  // Controlled_Buffer controlled_buffer_32
endmodule

module _1bitALU (
  input  carryIn,
  input  oparand1,
  input  operand2,
  input  [1:0] operation,
  output carryOut,
  output result
);

  wire and_1_out, n1_bit_fulladder_1_cout, n1_bit_fulladder_1_sum, not_1_out, not_2_out, or_1_out, xor_1_out;

  _1_Bit_FullAdder u_1_bit_fulladder_1 (
    .a(operand2), .b(oparand1), .carryIn(carryIn), .cout(n1_bit_fulladder_1_cout),
    .sum(n1_bit_fulladder_1_sum));
  and and_1 (and_1_out, operand2, oparand1);
  or or_1 (or_1_out, operand2, oparand1);
  xor xor_1 (xor_1_out, operand2, oparand1);
  not not_1 (not_1_out, operation[1]);
  not not_2 (not_2_out, operation[0]);
  Multiplexer #(.select(2), .enable("false")) multiplexer_1 (
    .in0(n1_bit_fulladder_1_sum), .in1(and_1_out), .in2(or_1_out), .in3(xor_1_out), .out(result),
    .sel(operation));
  and and_2 (carryOut, n1_bit_fulladder_1_cout, not_1_out, not_2_out);
endmodule

// ALU
module _18bitALU (
  input  Carry_In,
  input  [17:0] Operand_A,
  input  [17:0] Operand_B,
  input  [1:0] Operation,
  output [17:0] result,
  output overflow
);

  wire n1bitalu_1_carryout, n1bitalu_2_carryout, n1bitalu_3_carryout, n1bitalu_4_carryout,
       n1bitalu_5_carryout, n1bitalu_6_carryout, n1bitalu_7_carryout, n1bitalu_8_carryout,
       n1bitalu_9_carryout, n1bitalu_10_carryout, n1bitalu_11_carryout, n1bitalu_12_carryout,
       n1bitalu_13_carryout, n1bitalu_14_carryout, n1bitalu_15_carryout, n1bitalu_16_carryout,
       n1bitalu_17_carryout;

  _1bitALU u_1bitalu_1 (
    .result(result[0]), .oparand1(Operand_A[0]), .operand2(Operand_B[0]), .carryIn(Carry_In),
    .operation(Operation), .carryOut(n1bitalu_1_carryout));
  _1bitALU u_1bitalu_2 (
    .result(result[1]), .oparand1(Operand_A[1]), .operand2(Operand_B[1]), .carryIn(n1bitalu_1_carryout),
    .operation(Operation), .carryOut(n1bitalu_2_carryout));
  _1bitALU u_1bitalu_3 (
    .result(result[2]), .oparand1(Operand_A[2]), .operand2(Operand_B[2]), .carryIn(n1bitalu_2_carryout),
    .operation(Operation), .carryOut(n1bitalu_3_carryout));
  _1bitALU u_1bitalu_4 (
    .result(result[3]), .oparand1(Operand_A[3]), .operand2(Operand_B[3]), .carryIn(n1bitalu_3_carryout),
    .operation(Operation), .carryOut(n1bitalu_4_carryout));
  _1bitALU u_1bitalu_5 (
    .result(result[4]), .oparand1(Operand_A[4]), .operand2(Operand_B[4]), .carryIn(n1bitalu_4_carryout),
    .operation(Operation), .carryOut(n1bitalu_5_carryout));
  _1bitALU u_1bitalu_6 (
    .result(result[5]), .oparand1(Operand_A[5]), .operand2(Operand_B[5]), .carryIn(n1bitalu_5_carryout),
    .operation(Operation), .carryOut(n1bitalu_6_carryout));
  _1bitALU u_1bitalu_7 (
    .result(result[6]), .oparand1(Operand_A[6]), .operand2(Operand_B[6]), .carryIn(n1bitalu_6_carryout),
    .operation(Operation), .carryOut(n1bitalu_7_carryout));
  _1bitALU u_1bitalu_8 (
    .result(result[7]), .oparand1(Operand_A[7]), .operand2(Operand_B[7]), .carryIn(n1bitalu_7_carryout),
    .operation(Operation), .carryOut(n1bitalu_8_carryout));
  _1bitALU u_1bitalu_9 (
    .result(result[8]), .oparand1(Operand_A[8]), .operand2(Operand_B[8]), .carryIn(n1bitalu_8_carryout),
    .operation(Operation), .carryOut(n1bitalu_9_carryout));
  _1bitALU u_1bitalu_10 (
    .result(result[9]), .oparand1(Operand_A[9]), .operand2(Operand_B[9]), .carryIn(n1bitalu_9_carryout),
    .operation(Operation), .carryOut(n1bitalu_10_carryout));
  _1bitALU u_1bitalu_11 (
    .result(result[10]), .oparand1(Operand_A[10]), .operand2(Operand_B[10]), .carryIn(n1bitalu_10_carryout),
    .operation(Operation), .carryOut(n1bitalu_11_carryout));
  _1bitALU u_1bitalu_12 (
    .result(result[11]), .oparand1(Operand_A[11]), .operand2(Operand_B[11]), .carryIn(n1bitalu_11_carryout),
    .operation(Operation), .carryOut(n1bitalu_12_carryout));
  _1bitALU u_1bitalu_13 (
    .result(result[12]), .oparand1(Operand_A[12]), .operand2(Operand_B[12]), .carryIn(n1bitalu_12_carryout),
    .operation(Operation), .carryOut(n1bitalu_13_carryout));
  _1bitALU u_1bitalu_14 (
    .result(result[13]), .oparand1(Operand_A[13]), .operand2(Operand_B[13]), .carryIn(n1bitalu_13_carryout),
    .operation(Operation), .carryOut(n1bitalu_14_carryout));
  _1bitALU u_1bitalu_15 (
    .result(result[14]), .oparand1(Operand_A[14]), .operand2(Operand_B[14]), .carryIn(n1bitalu_14_carryout),
    .operation(Operation), .carryOut(n1bitalu_15_carryout));
  _1bitALU u_1bitalu_16 (
    .result(result[15]), .oparand1(Operand_A[15]), .operand2(Operand_B[15]), .carryIn(n1bitalu_15_carryout),
    .operation(Operation), .carryOut(n1bitalu_16_carryout));
  _1bitALU u_1bitalu_17 (
    .result(result[16]), .oparand1(Operand_A[16]), .operand2(Operand_B[16]), .carryIn(n1bitalu_16_carryout),
    .operation(Operation), .carryOut(n1bitalu_17_carryout));
  _1bitALU u_1bitalu_18 (
    .result(result[17]), .oparand1(Operand_A[17]), .operand2(Operand_B[17]), .carryIn(n1bitalu_17_carryout),
    .operation(Operation), .carryOut(overflow));

  // Other names for the same wires on the sheet: A0 = Operand_A[0]; A1 = Operand_A[1]; A2 = Operand_A[2];
  //   A3 = Operand_A[3]; A4 = Operand_A[4]; A5 = Operand_A[5]; A6 = Operand_A[6]; A7 = Operand_A[7];
  //   A8 = Operand_A[8]; A9 = Operand_A[9]; A10 = Operand_A[10]; A11 = Operand_A[11]; A12 = Operand_A[12];
  //   A13 = Operand_A[13]; A14 = Operand_A[14]; A15 = Operand_A[15]; A16 = Operand_A[16]; A17 = Operand_A[17];
  //   B0 = Operand_B[0]; B1 = Operand_B[1]; B2 = Operand_B[2]; B3 = Operand_B[3]; B4 = Operand_B[4];
  //   B5 = Operand_B[5]; B6 = Operand_B[6]; B7 = Operand_B[7]; B8 = Operand_B[8]; B9 = Operand_B[9];
  //   B10 = Operand_B[10]; B11 = Operand_B[11]; B12 = Operand_B[12]; B13 = Operand_B[13]; B14 = Operand_B[14];
  //   B15 = Operand_B[15]; B16 = Operand_B[16]; B17 = Operand_B[17]
endmodule

module _1bitComparator (
  input  gt_in,
  input  a,
  input  b,
  input  lt_in,
  output gt,
  output eq,
  output lt
);

  wire and_1_out, and_2_out, and_3_out, and_4_out, not_1_out, not_2_out, not_3_out, not_4_out, not_5_out,
       not_6_out, or_1_out, or_2_out, or_3_out;

  not not_1 (not_1_out, a);
  not not_2 (not_2_out, b);
  and and_1 (and_1_out, a, not_2_out);
  and and_2 (and_2_out, a, b);
  or or_1 (or_1_out, and_2_out, and_3_out);
  and and_3 (and_3_out, not_1_out, not_2_out);
  and and_4 (and_4_out, not_1_out, b);
  or or_2 (or_2_out, gt_in, and_1_out);
  not not_3 (not_3_out, gt_in);
  and and_5 (eq, not_3_out, or_1_out, not_4_out);
  not not_4 (not_4_out, lt_in);
  or or_3 (or_3_out, and_4_out, lt_in);
  and and_6 (gt, or_2_out, not_5_out);
  not not_5 (not_5_out, lt_in);
  not not_6 (not_6_out, gt_in);
  and and_7 (lt, not_6_out, or_3_out);
endmodule

module _18bitComparator (
  input  [17:0] in_1,
  input  [17:0] in_2,
  output gt,
  output eq,
  output lt
);

  wire and_1_out, and_2_out, n1bitcomparator_1_gt, n1bitcomparator_1_lt, n1bitcomparator_2_gt,
       n1bitcomparator_2_lt, n1bitcomparator_3_gt, n1bitcomparator_3_lt, n1bitcomparator_4_gt,
       n1bitcomparator_4_lt, n1bitcomparator_5_gt, n1bitcomparator_5_lt, n1bitcomparator_6_gt,
       n1bitcomparator_6_lt, n1bitcomparator_7_gt, n1bitcomparator_7_lt, n1bitcomparator_8_gt,
       n1bitcomparator_8_lt, n1bitcomparator_9_gt, n1bitcomparator_9_lt, n1bitcomparator_10_gt,
       n1bitcomparator_10_lt, n1bitcomparator_11_gt, n1bitcomparator_11_lt, n1bitcomparator_12_gt,
       n1bitcomparator_12_lt, n1bitcomparator_13_gt, n1bitcomparator_13_lt, n1bitcomparator_14_gt,
       n1bitcomparator_14_lt, n1bitcomparator_15_gt, n1bitcomparator_15_lt, n1bitcomparator_16_gt,
       n1bitcomparator_16_lt, not_1_out, not_2_out;

  not not_1 (not_1_out, in_1[17]);
  and and_1 (and_1_out, not_1_out, in_2[17]);
  and and_2 (and_2_out, in_1[17], not_2_out);
  not not_2 (not_2_out, in_2[17]);
  _1bitComparator u_1bitcomparator_1 (
    .gt(n1bitcomparator_1_gt), .lt(n1bitcomparator_1_lt), .gt_in(and_1_out), .a(in_1[16]), .b(in_2[16]),
    .lt_in(and_2_out));  // open: eq
  _1bitComparator u_1bitcomparator_2 (
    .gt(n1bitcomparator_2_gt), .lt(n1bitcomparator_2_lt), .gt_in(n1bitcomparator_3_gt), .a(in_1[14]),
    .b(in_2[14]), .lt_in(n1bitcomparator_3_lt));  // open: eq
  _1bitComparator u_1bitcomparator_3 (
    .gt(n1bitcomparator_3_gt), .lt(n1bitcomparator_3_lt), .gt_in(n1bitcomparator_1_gt), .a(in_1[15]),
    .b(in_2[15]), .lt_in(n1bitcomparator_1_lt));  // open: eq
  _1bitComparator u_1bitcomparator_4 (
    .gt(n1bitcomparator_4_gt), .lt(n1bitcomparator_4_lt), .gt_in(n1bitcomparator_2_gt), .a(in_1[13]),
    .b(in_2[13]), .lt_in(n1bitcomparator_2_lt));  // open: eq
  _1bitComparator u_1bitcomparator_5 (
    .gt(n1bitcomparator_5_gt), .lt(n1bitcomparator_5_lt), .gt_in(n1bitcomparator_4_gt), .a(in_1[12]),
    .b(in_2[12]), .lt_in(n1bitcomparator_4_lt));  // open: eq
  _1bitComparator u_1bitcomparator_6 (
    .gt(n1bitcomparator_6_gt), .lt(n1bitcomparator_6_lt), .gt_in(n1bitcomparator_5_gt), .a(in_1[11]),
    .b(in_2[11]), .lt_in(n1bitcomparator_5_lt));  // open: eq
  _1bitComparator u_1bitcomparator_7 (
    .gt(n1bitcomparator_7_gt), .lt(n1bitcomparator_7_lt), .gt_in(n1bitcomparator_8_gt), .a(in_1[9]),
    .b(in_2[9]), .lt_in(n1bitcomparator_8_lt));  // open: eq
  _1bitComparator u_1bitcomparator_8 (
    .gt(n1bitcomparator_8_gt), .lt(n1bitcomparator_8_lt), .gt_in(n1bitcomparator_6_gt), .a(in_1[10]),
    .b(in_2[10]), .lt_in(n1bitcomparator_6_lt));  // open: eq
  _1bitComparator u_1bitcomparator_9 (
    .gt(n1bitcomparator_9_gt), .lt(n1bitcomparator_9_lt), .gt_in(n1bitcomparator_7_gt), .a(in_1[8]),
    .b(in_2[8]), .lt_in(n1bitcomparator_7_lt));  // open: eq
  _1bitComparator u_1bitcomparator_10 (
    .gt(n1bitcomparator_10_gt), .lt(n1bitcomparator_10_lt), .gt_in(n1bitcomparator_9_gt), .a(in_1[7]),
    .b(in_2[7]), .lt_in(n1bitcomparator_9_lt));  // open: eq
  _1bitComparator u_1bitcomparator_11 (
    .gt(n1bitcomparator_11_gt), .lt(n1bitcomparator_11_lt), .gt_in(n1bitcomparator_10_gt), .a(in_1[6]),
    .b(in_2[6]), .lt_in(n1bitcomparator_10_lt));  // open: eq
  _1bitComparator u_1bitcomparator_12 (
    .gt(n1bitcomparator_12_gt), .lt(n1bitcomparator_12_lt), .gt_in(n1bitcomparator_11_gt), .a(in_1[5]),
    .b(in_2[5]), .lt_in(n1bitcomparator_11_lt));  // open: eq
  _1bitComparator u_1bitcomparator_13 (
    .gt(n1bitcomparator_13_gt), .lt(n1bitcomparator_13_lt), .gt_in(n1bitcomparator_14_gt), .a(in_1[3]),
    .b(in_2[3]), .lt_in(n1bitcomparator_14_lt));  // open: eq
  _1bitComparator u_1bitcomparator_14 (
    .gt(n1bitcomparator_14_gt), .lt(n1bitcomparator_14_lt), .gt_in(n1bitcomparator_12_gt), .a(in_1[4]),
    .b(in_2[4]), .lt_in(n1bitcomparator_12_lt));  // open: eq
  _1bitComparator u_1bitcomparator_15 (
    .gt(n1bitcomparator_15_gt), .lt(n1bitcomparator_15_lt), .gt_in(n1bitcomparator_16_gt), .a(in_1[1]),
    .b(in_2[1]), .lt_in(n1bitcomparator_16_lt));  // open: eq
  _1bitComparator u_1bitcomparator_16 (
    .gt(n1bitcomparator_16_gt), .lt(n1bitcomparator_16_lt), .gt_in(n1bitcomparator_13_gt), .a(in_1[2]),
    .b(in_2[2]), .lt_in(n1bitcomparator_13_lt));  // open: eq
  _1bitComparator u_1bitcomparator_17 (
    .gt(gt), .eq(eq), .lt(lt), .gt_in(n1bitcomparator_15_gt), .a(in_1[0]), .b(in_2[0]),
    .lt_in(n1bitcomparator_15_lt));
endmodule

module produceNZP (
  input  [3:0] Opcode,
  output n,
  output z,
  output p
);

  wire and_1_out, and_2_out, and_3_out, and_4_out, and_5_out, and_6_out, and_7_out, not_1_out, not_2_out,
       not_3_out, not_4_out, not_5_out, not_6_out;

  and and_1 (and_1_out, Opcode[3], Opcode[2], not_1_out, Opcode[0]);
  not not_1 (not_1_out, Opcode[1]);
  and and_2 (and_2_out, Opcode[3], Opcode[2], Opcode[1], Opcode[0]);
  not not_2 (not_2_out, Opcode[2]);
  and and_3 (and_3_out, Opcode[3], not_2_out, Opcode[1], Opcode[0]);
  and and_4 (and_4_out, Opcode[3], Opcode[2], Opcode[1], not_3_out);
  not not_3 (not_3_out, Opcode[0]);
  and and_5 (and_5_out, Opcode[3], Opcode[2], Opcode[1], Opcode[0]);
  and and_6 (and_6_out, Opcode[3], Opcode[2], not_4_out, not_5_out);
  not not_4 (not_4_out, Opcode[1]);
  not not_5 (not_5_out, Opcode[0]);
  and and_7 (and_7_out, Opcode[3], Opcode[2], Opcode[1], not_6_out);
  not not_6 (not_6_out, Opcode[0]);
  or or_1 (n, and_1_out, and_2_out);
  or or_2 (z, and_3_out, and_4_out, and_5_out);
  or or_3 (p, and_6_out, and_7_out);
endmodule

module ControlUnit (
  input  in_1,
  input  [3:0] opcode,
  output PcEnable,
  output we,
  output Load,
  output src1,
  output src2,
  output store,
  output jump,
  output brach
);

  wire and_1_out, and_2_out, and_3_out, and_4_out, and_5_out, and_6_out, not_1_out, not_2_out, not_3_out,
       not_4_out, not_5_out, not_6_out, not_7_out, not_8_out, or_1_out, or_2_out, or_3_out, or_4_out;

  Register #(.width(1)) stateRegister (.D(not_1_out), .Q(PcEnable), .clk(in_1));  // open: en, clr
  not not_1 (not_1_out, PcEnable);
  not not_2 (not_2_out, opcode[2]);
  not not_3 (not_3_out, opcode[1]);
  not not_4 (not_4_out, opcode[0]);
  and and_1 (and_1_out, opcode[3], opcode[0]);
  and and_2 (and_2_out, opcode[3], opcode[2]);
  and and_3 (and_3_out, opcode[3], opcode[1], opcode[0]);
  not not_5 (not_5_out, opcode[2]);
  and and_4 (and_4_out, opcode[3], not_5_out, not_6_out, opcode[0]);
  not not_6 (not_6_out, opcode[1]);
  and and_5 (and_5_out, opcode[3], opcode[1]);
  not not_7 (not_7_out, opcode[3]);
  or or_1 (or_1_out, not_7_out, and_6_out);
  and and_6 (and_6_out, opcode[3], not_2_out, not_3_out, not_4_out);
  or or_2 (or_2_out, and_1_out, and_2_out);
  or or_3 (or_3_out, and_2_out, and_3_out);
  or or_4 (or_4_out, and_2_out, and_5_out);
  not not_8 (not_8_out, PcEnable);
  and and_7 (we, not_8_out, or_1_out);
  and and_8 (Load, not_8_out, and_6_out);
  and and_9 (src1, not_8_out, or_2_out);
  and and_10 (src2, not_8_out, or_3_out);
  and and_11 (store, not_8_out, and_4_out);
  and and_12 (jump, not_8_out, or_4_out);
  and and_13 (brach, not_8_out, or_3_out);
endmodule

module deneme (
  input  [7:0] in_1,
  input  [7:0] in_2,
  output [7:0] out_3
);

  Adder adder_1 (.a(in_1), .b(in_2), .out(out_3));  // open: cin, cout
endmodule

module _1_Bit_FullAdder (
  input  a,
  input  b,
  input  carryIn,
  output cout,
  output sum
);

  wire and_1_out, and_2_out, and_3_out, and_4_out, and_5_out, and_6_out, and_7_out, not_1_out, not_2_out,
       not_3_out, not_4_out, not_5_out, not_6_out;

  and and_1 (and_1_out, carryIn, b);
  and and_2 (and_2_out, a, b);
  or or_1 (cout, and_1_out, and_2_out, and_3_out);
  and and_3 (and_3_out, carryIn, a);
  not not_1 (not_1_out, a);
  not not_2 (not_2_out, carryIn);
  and and_4 (and_4_out, not_2_out, b, not_1_out);
  not not_3 (not_3_out, carryIn);
  not not_4 (not_4_out, b);
  and and_5 (and_5_out, not_3_out, not_4_out, a);
  or or_2 (sum, and_4_out, and_5_out, and_6_out, and_7_out);
  not not_5 (not_5_out, a);
  not not_6 (not_6_out, b);
  and and_6 (and_6_out, carryIn, not_6_out, not_5_out);
  and and_7 (and_7_out, carryIn, b, a);
endmodule

module _14bitAdder (
  input  [13:0] a,
  input  [13:0] b,
  output [13:0] \output ,
  output c_out
);

  wire n1_bit_fulladder_1_cout, n1_bit_fulladder_2_cout, n1_bit_fulladder_3_cout, n1_bit_fulladder_4_cout,
       n1_bit_fulladder_5_cout, n1_bit_fulladder_6_cout, n1_bit_fulladder_7_cout, n1_bit_fulladder_8_cout,
       n1_bit_fulladder_9_cout, n1_bit_fulladder_10_cout, n1_bit_fulladder_11_cout, n1_bit_fulladder_12_cout,
       n1_bit_fulladder_13_cout;

  _1_Bit_FullAdder u_1_bit_fulladder_1 (
    .a(a[0]), .b(b[0]), .carryIn(1'b0), .cout(n1_bit_fulladder_1_cout), .sum(\output [0]));
  _1_Bit_FullAdder u_1_bit_fulladder_2 (
    .a(a[1]), .b(b[1]), .carryIn(n1_bit_fulladder_1_cout), .cout(n1_bit_fulladder_2_cout), .sum(\output [1]));
  _1_Bit_FullAdder u_1_bit_fulladder_3 (
    .a(a[2]), .b(b[2]), .carryIn(n1_bit_fulladder_2_cout), .cout(n1_bit_fulladder_3_cout), .sum(\output [2]));
  _1_Bit_FullAdder u_1_bit_fulladder_4 (
    .a(a[3]), .b(b[3]), .carryIn(n1_bit_fulladder_3_cout), .cout(n1_bit_fulladder_4_cout), .sum(\output [3]));
  _1_Bit_FullAdder u_1_bit_fulladder_5 (
    .a(a[4]), .b(b[4]), .carryIn(n1_bit_fulladder_4_cout), .cout(n1_bit_fulladder_5_cout), .sum(\output [4]));
  _1_Bit_FullAdder u_1_bit_fulladder_6 (
    .a(a[5]), .b(b[5]), .carryIn(n1_bit_fulladder_5_cout), .cout(n1_bit_fulladder_6_cout), .sum(\output [5]));
  _1_Bit_FullAdder u_1_bit_fulladder_7 (
    .a(a[6]), .b(b[6]), .carryIn(n1_bit_fulladder_6_cout), .cout(n1_bit_fulladder_7_cout), .sum(\output [6]));
  _1_Bit_FullAdder u_1_bit_fulladder_8 (
    .a(a[7]), .b(b[7]), .carryIn(n1_bit_fulladder_7_cout), .cout(n1_bit_fulladder_8_cout), .sum(\output [7]));
  _1_Bit_FullAdder u_1_bit_fulladder_9 (
    .a(a[8]), .b(b[8]), .carryIn(n1_bit_fulladder_8_cout), .cout(n1_bit_fulladder_9_cout), .sum(\output [8]));
  _1_Bit_FullAdder u_1_bit_fulladder_10 (
    .a(a[9]), .b(b[9]), .carryIn(n1_bit_fulladder_9_cout), .cout(n1_bit_fulladder_10_cout), .sum(\output [9]));
  _1_Bit_FullAdder u_1_bit_fulladder_11 (
    .a(a[10]), .b(b[10]), .carryIn(n1_bit_fulladder_10_cout), .cout(n1_bit_fulladder_11_cout),
    .sum(\output [10]));
  _1_Bit_FullAdder u_1_bit_fulladder_12 (
    .a(a[11]), .b(b[11]), .carryIn(n1_bit_fulladder_11_cout), .cout(n1_bit_fulladder_12_cout),
    .sum(\output [11]));
  _1_Bit_FullAdder u_1_bit_fulladder_13 (
    .a(a[12]), .b(b[12]), .carryIn(n1_bit_fulladder_12_cout), .cout(n1_bit_fulladder_13_cout),
    .sum(\output [12]));
  _1_Bit_FullAdder u_1_bit_fulladder_14 (
    .a(a[13]), .b(b[13]), .carryIn(n1_bit_fulladder_13_cout), .cout(c_out), .sum(\output [13]));
endmodule
